# Fritzing sketch example_schematic (saved by Fritzing 0.9.5d)

parts:
  Mod1 = Raspberry Pi Pico
  Part1 = Shift Register Breakout - 74HC595
  7_Segment1 = 7 Segment Display
  Part2 = Shift Register Breakout - 74HC595
  7_Segment2 = 7 Segment Display
  Part3 = Shift Register Breakout - 74HC595
  7_Segment3 = 7 Segment Display

nets:
  N1: Mod1.pin_4, Part1.CLOCK, Part2.CLOCK, Part3.CLOCK
  N2: Mod1.pin_5, Part1.SERIAL_IN
  N3: Mod1.pin_6, Part1.LATCH_CLOCK, Part2.LATCH_CLOCK, Part3.LATCH_CLOCK
  GND: Mod1.pin_23, Mod1.pin_42, Part1.GND, Part1./RESET, Part1./OUTPUT_ENABLE, 7_Segment1.common_cathode, Part2.GND, Part2./RESET, Part2./OUTPUT_ENABLE, 7_Segment2.common_cathode, Part3.GND, Part3./RESET, Part3./OUTPUT_ENABLE, 7_Segment3.common_cathode
  VCC: Mod1.pin_36, Part1.VCC, Part2.VCC, Part3.VCC
  N4: Part1.QA, 7_Segment1.Segment_A
  N5: Part1.QB, 7_Segment1.Segment_B
  N6: Part1.QC, 7_Segment1.Segment_C
  N7: Part1.QD, 7_Segment1.Segment_D
  N8: Part1.QE, 7_Segment1.Segment_E
  N9: Part1.QF, 7_Segment1.Segment_F
  N10: Part1.QG, 7_Segment1.Segment_G
  N11: Part1.QH, 7_Segment1.Segment_DP
  N12: Part1.SERIAL_OUT, Part2.SERIAL_IN
  N13: Part2.QA, 7_Segment2.Segment_A
  N14: Part2.QB, 7_Segment2.Segment_B
  N15: Part2.QC, 7_Segment2.Segment_C
  N16: Part2.QD, 7_Segment2.Segment_D
  N17: Part2.QE, 7_Segment2.Segment_E
  N18: Part2.QF, 7_Segment2.Segment_F
  N19: Part2.QG, 7_Segment2.Segment_G
  N20: Part2.QH, 7_Segment2.Segment_DP
  N21: Part2.SERIAL_OUT, Part3.SERIAL_IN
  N22: Part3.QA, 7_Segment3.Segment_A
  N23: Part3.QB, 7_Segment3.Segment_B
  N24: Part3.QC, 7_Segment3.Segment_C
  N25: Part3.QD, 7_Segment3.Segment_D
  N26: Part3.QE, 7_Segment3.Segment_E
  N27: Part3.QF, 7_Segment3.Segment_F
  N28: Part3.QG, 7_Segment3.Segment_G
  N29: Part3.QH, 7_Segment3.Segment_DP

notes:
  sdi
  sck
  latch
  this grey box is a single module

custom parts:
  Raspberry Pi Pico: Raspberry Pi Pico. Based around the RP2040 microcontroller the Pico is a low cost microcontroller device bringing Raspberry Pi quality, cost, and easy of use to the microcontroller space. Jan 2021, Split part in to two versions: tht (this one) and SMD. This one will drill holes for a .1 in header in pcb to allow plugging in the module as well as providing pads to solder the module to the top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
